# Fritzing sketch circuit (saved by Fritzing 0.9.3b)
breadboards: 2

parts:
  U1 = ATTINY13 [package=dip]
  DHT1 = DHT11 Humitidy and Temperature Sensor
  R1 = Resistor [tolerance=±5% resistance=10k package=THT]
  BAT1 = Battery Holders [package=battcon_245mm_pth]
  Part1 = NRF24L01+ Breakout Board
  R2 = Resistor [tolerance=±5% resistance=4.7k package=THT]
  R3 = Resistor [tolerance=±5% resistance=220 package=THT]
  C2 = Ceramic Capacitor [capacitance=1µF package="100 mil [THT, multilayer]"]
  C3 = Ceramic Capacitor [capacitance=10µF package="100 mil [THT, multilayer]"]
  J1 = female pin header, 8 pins [form="♀ (female)"]

nets:
  dht11: U1.PB3(ADC3), DHT1.DATA, R1.Pin_1
  GND/nRF_Gnd: U1.GND, DHT1.GND, BAT1.-, Part1.GND, C2.0, C3.0, J1.pin2
  nRF_MOSI: U1.PB0(MOSI), Part1.MOSI, R2.Pin_1, J1.pin6
  nRF_SCK: U1.PB2(SCK_ADC1), Part1.SCK, R3.Pin_1, J1.pin5
  3V/nRF_CE/nRF_Vcc: U1.VCC, DHT1.VDD, R1.Pin_0, BAT1.+, Part1.VCC, Part1.CE, C3.1, J1.pin1, J1.pin3
  nRF_CS: Part1.CS, R3.Pin_0, C2.1, J1.pin4
  nRF_MISO: Part1.MISO, R2.Pin_0, J1.pin7
  nRF_IRQ: Part1.IRQ, J1.pin8

custom parts:
  DHT11 Humitidy and Temperature Sensor: DHT11 Humidity and Temperature Sensor
